# Fritzing sketch fuglekameraten (saved by Fritzing 0.9.0b)
breadboards: 1

parts:
  R1 = Resistor [tolerance=±5% resistance=330 package=THT]
  LED1 = LED - 5mm [color="Red (633nm)" package="5 mm [THT]"]
  Raspberry_Pi_B_rev1 = Raspberry Pi B rev2
  R2 = Resistor [tolerance=±5% resistance=1k package=THT]
  R3 = Resistor [tolerance=±5% resistance=1k package=THT]
  R4 = Photocell (LDR) [package=THT]
  C1 = Ceramic Capacitor [capacitance=100nF package="100 mil [THT, multilayer]"]

nets:
  N1: R1.Pin_0, Raspberry_Pi_B_rev1.GND, C1.1
  N2: R1.Pin_1, LED1.cathode
  N3: LED1.anode, Raspberry_Pi_B_rev1.GPIO_2
  N4: Raspberry_Pi_B_rev1.GPIO_3, R2.Pin_1
  N5: Raspberry_Pi_B_rev1.GPIO_4, R3.Pin_1
  N6: R2.Pin_0, R4.pin_0
  N7: R3.Pin_0, R4.pin_1, C1.0
